# Fritzing sketch final_stm (saved by Fritzing 1.0.3b)
breadboards: 2

parts:
  R5 = Resistor [tolerance=±5% power=0.25W resistance=2200 package=THT]
  R6 = Resistor [tolerance=±5% power=0.25W resistance=470 package=THT]
  S1 = Pushbutton [package="[THT]"]
  LCD1 = LCD screen
  R7 = Resistor [tolerance=±5% power=0.25W resistance=470 package=THT]
  R8 = Resistor [tolerance=±5% power=0.25W resistance=470 package=THT]
  LED1 = RGB LED (com. cathode, rbg) [color="Red (633nm)" current=0.030A package="5 mm [THT]"]
  T1 = LM35 Temperature Sensor [package="TO92 [THT]"]
  J1 = Piezo Speaker
  LED2 = smd LED [color="Red (633nm)" package="0805 [SMD]"]
  R9 = Resistor [tolerance=±5% power=0.25W resistance=470 package=THT]
  R10 = Resistor [tolerance=±5% power=0.25W resistance=1000 package=THT]
  R11 = Rotary Potentiometer (Large) [maximum_resistance=100kΩ knob_status=50% power=0.5W package=THT]
  U1 = Carte NUCLEO H755ZI-Q
  J2 = Basic Servo
  U2 = LIPO-110mAh [package=lipo-110]

nets:
  N1: R5.Pin_0, LCD1.V0
  GND: R5.Pin_1, S1.Pin_1, S1.Pin_2, LCD1.VSS, LCD1.R/W, LCD1.LED-, LED1.common_cathode, T1.GND, J1.pin1, LED2.cathode, R11.leg2, U1.GND, J2.gnd, U2.-
  N2: R6.Pin_0, U1.D1(PG14)
  N3: R6.Pin_1, LED1.red_anode
  N4: S1.Pin_3, S1.Pin_4, U1.D-10
  VDD: LCD1.VDD, R10.Pin_1, R11.leg1, U1.5V
  N5: LCD1.RS, U1.D-13_(PA5)
  N6: LCD1.E, U1.D-12_(PA6)
  N7: LCD1.DB4, U1.D4(PF14)
  N8: LCD1.DB5, U1.D5(PE11)
  N9: LCD1.DB6, U1.D6(PE9)
  N10: LCD1.DB7, U1.D7(PF13)
  N11: LCD1.LED+, R10.Pin_0
  N12: R7.Pin_0, U1.D2(PF15)
  N13: R7.Pin_1, LED1.blue_anode
  N14: R8.Pin_0, U1.D3(PE13)
  N15: R8.Pin_1, LED1.green_anode
  N16: T1.+Vs, U1.pin_86
  N17: T1.Vout, U1.A0
  N18: J1.pin2, U1.D-8
  N19: LED2.anode, R9.Pin_1
  N20: R9.Pin_0, U1.D-9
  N21: U1.D-11, J2.pulse

custom parts:
  Carte NUCLEO H755ZI-Q: Carte prototype double coeurs ARM
